# Fritzing sketch TLCv1 (saved by Fritzing 0.9.3b)
circuit board: 6.48869cm x 4.40104cm
breadboards: 1

parts:
  <--_Status = RGB LED (com. cathode, rbg) [package="5 mm [THT]"]
  Effect_Toggle = Header 2 [package=molex-1x2_lock]
  Pwr_Swtch = Header 2 [package=molex-1x2_lock]
  Power_5-12v = Header 2 [package=molex-1x2_lock]
  Config = DIP Switch 4 Position [package=dipswitch-04]
  5v_or_3_3v = female pin header, 3 pins [form="♀ (female)"]
  LED_Strip = Header 3 [package=molex-1x3_lock]
  100uf = Capacitor Polarized [package=cpol-radial-100uf-25v]
  Sensor_-> = Header 3 [package=molex-1x3_lock]
  nRF24L01 = Generic shrouded header - 8 pins [form="♂ (shrouded male)" package=THT]
  R1 = Resistor [tolerance=±5% resistance=220 package=THT]
  R2 = Resistor [tolerance=±5% resistance=220 package=THT]
  R3 = Resistor [tolerance=±5% resistance=220 package=THT]
  J2 = female pin header, 7 pins [form="♀ (female)"]
  Nano = Arduino Nano (Rev3.0)

nets:
  N1: <--_Status.red_anode, R3.Pin_1
  N2: <--_Status.common_cathode, Effect_Toggle.2, Power_5-12v.2, Config.5, Config.6, Config.7, Config.8, LED_Strip.3, 100uf.-, Sensor_->.1, nRF24L01.grd, Nano.GND
  N3: <--_Status.blue_anode, R1.Pin_1
  N4: <--_Status.green_anode, R2.Pin_1
  N5: Effect_Toggle.1, Nano.D6
  N6: Pwr_Swtch.1, Nano.VIN
  N7: Pwr_Swtch.2, Power_5-12v.1
  N8: Config.1, Nano.D2
  N9: Config.2, Nano.D3
  N10: Config.3, Nano.D4
  N11: Config.4, Nano.D5
  N12: 5v_or_3_3v.pin1, J2.pin6, Nano.3V3
  N13: 5v_or_3_3v.pin2, 100uf.+, nRF24L01.v+
  N14: 5v_or_3_3v.pin3, LED_Strip.1, Sensor_->.2, J2.pin7, Nano.5V
  N15: LED_Strip.2, Nano.D8
  N16: Sensor_->.3, Nano.A7
  N17: nRF24L01.ce, Nano.D9
  N18: nRF24L01.sck, Nano.D13/SCK
  N19: nRF24L01.miso, Nano.D12/MISO
  N20: nRF24L01.mosi, Nano.D11/MOSI
  N21: nRF24L01.csn, Nano.D10
  N22: R1.Pin_0, Nano.A1
  N23: R2.Pin_0, Nano.A2
  N24: R3.Pin_0, Nano.A0
  N25: J2.pin1, Nano.D7
  N26: J2.pin2, Nano.A3
  N27: J2.pin3, Nano.A4
  N28: J2.pin4, Nano.A5
  N29: J2.pin5, Nano.A6

notes:
  Totally Legit Camp: Terrific LED Controller
  hecho en mexico

custom parts:
  Generic shrouded header - 8 pins: Generic shrouded header
